// Logisim project A1_G3_Final_final.circ as structural Verilog: 1 circuit, main circuit main
module main (
  input  A0,
  input  A1,
  input  A2,
  input  A3,
  input  B0,
  input  B1,
  input  B2,
  input  B3,
  input  S0,
  input  S1,
  input  S2,
  output Flag_C,
  output Flag_Z,
  output FlagS,
  output Flag_V,
  output S0_2,
  output S1_2,
  output S2_2,
  output S3
);

  wire n7404_1_p2, n7404_1_p3, n7404_1_p6, n7404_1_p7, n7404_1_p10, n7404_1_p11, n7404_2_p7, n7408_2_p3,
       n7408_2_p6, n7408_2_p11, n7408_2_p14, n7408_3_p3, n7408_3_p5, n7408_3_p6, n7408_3_p10, n7408_3_p11,
       n7408_3_p13, n7408_3_p14, n7408_4_p2, n7408_4_p3, n7408_4_p4, n7408_4_p5, n7408_4_p6, n7408_4_p12,
       n7432_1_p1, n7432_1_p3, n7432_1_p4, n7432_1_p6, n7432_1_p8, n7432_1_p10, n7432_1_p11, n7432_2_p8,
       n7432_2_p17, n7486_1_p4, n7486_1_p7, n7486_1_p9, n7486_1_p13, n7486_1_p16;

  // _7404 7404_1: pin names not known; wires that end beside it: 1'b0, n7404_1_p2, n7404_1_p3, S0, B2, n7404_1_p6, n7404_1_p7, S2, B1, n7404_1_p10, n7404_1_p11, B3, B0, 1'b1
  // _7432 7432_1: pin names not known; wires that end beside it: n7432_1_p1, A0, n7432_1_p3, n7432_1_p4, A1, n7432_1_p6, 1'b1, n7432_1_p8, A2, n7432_1_p10, n7432_1_p11, A3
  // _7486 7486_1: pin names not known; wires that end beside it: 1'b0, S0, n7404_1_p11, n7486_1_p4, n7404_1_p7, S0, n7486_1_p7, 1'b0, n7486_1_p9, 1'b1, n7404_1_p3, S0, n7486_1_p13, n7404_1_p10, S0, n7486_1_p16
  // _7408 7408_1: pin names not known; wires that end beside it: n7486_1_p4, S2, n7432_1_p1, n7486_1_p7, S2, n7432_1_p4, 1'b0, 1'b1, n7486_1_p13, S2, n7432_1_p8, n7486_1_p16, S2, n7432_1_p11
  // _7408 7408_2: pin names not known; wires that end beside it: n7404_1_p2, n7404_1_p11, n7408_2_p3, n7404_1_p7, n7404_1_p2, n7408_2_p6, 1'b0, 1'b1, n7404_1_p3, n7404_1_p2, n7408_2_p11, n7404_1_p10, n7404_1_p2, n7408_2_p14
  // _7408 7408_3: pin names not known; wires that end beside it: n7404_1_p6, S1, n7408_3_p3, n7404_1_p6, n7408_3_p5, n7408_3_p6, 1'b0, 1'b1, n7404_1_p6, n7408_3_p10, n7408_3_p11, n7404_1_p6, n7408_3_p13, n7408_3_p14
  // _7408 7408_4: pin names not known; wires that end beside it: n7408_3_p13, n7408_4_p2, n7408_4_p3, n7408_4_p4, n7408_4_p5, n7408_4_p6, 1'b0, 1'b1, n7408_4_p4, n7404_1_p6, Flag_C, n7408_4_p12, n7404_1_p6, Flag_V
  // _7404 7404_2: pin names not known; wires that end beside it: n7408_3_p13, n7408_4_p5, n7408_4_p4, n7408_4_p2, 1'b0, 1'b1, n7404_2_p7, Flag_Z
  // _7483 7483_1: pin names not known; wires that end beside it: n7432_1_p6, n7408_3_p6, 1'b1, 1'b1, n7408_3_p5, 1'b0, 1'b0, n7408_2_p6, S1_2, n7408_3_p10, n7408_3_p3, 1'b0, n7408_2_p3, n7432_1_p3, S0_2
  // _7483 7483_2: pin names not known; wires that end beside it: n7486_1_p9, n7408_3_p14, 1'b1, 1'b1, n7408_2_p14, FlagS, n7408_4_p4, n7408_3_p11, 1'b0
  // _7432 7432_2: pin names not known; wires that end beside it: n7408_3_p13, 1'b0, 1'b0, n7408_4_p3, n7408_4_p6, n7408_4_p12, S0_2, n7432_2_p8, n7404_2_p7, 1'b0, n7408_2_p11, n7432_1_p10, S2_2, 1'b1, FlagS, S2_2, n7432_2_p17, n7432_2_p17, S1_2, n7432_2_p8

  assign S3 = FlagS;

  // Notes on the sheet:
  //   x0
  //   x2
  //   x3
  //   x1
  //   y0
  //   y1
  //   y3
  //   y2
  //   Z
  //   VCC RAIL
  //   GND RAIL
  //   zero
  //   Cin0
  //   X0
  //   Y0
  //   Cin1
  //   Cin2
  //   X2
  //   Y3
  //   Cin3
  //   X3
  //   X1
  //   y1
  //   Y2
  //   Cout0
  //   Cout1
  //   Cout2
  //   Cout3
endmodule
