// Logisim project A1_G3_3.circ as structural Verilog: 15 circuits, main circuit main
module main (
  input  [31:0] Input1,
  input  [31:0] Input2,
  output [31:0] Output,
  output UnderFlow,
  output Overflow
);

  wire ExpoDiff_compare, n7404_1__2__1y, n7404_2__2__1y, n7404_2__4__2y, n7408_1__3__1y, n7408_1__6__2y,
       n7408_1__8__3y, n7408_1__11__4y, n7408_2__3__1y, n7408_2__6__2y, n7408_2__11__4y, n7432_1__3__1y,
       n7432_1__6__2y, n7432_1__8__3y, n7432_1__11__4y, n74153_1__7__y1, n74153_1__9__y2,
       resultnegate_1_signedbit, shamt_1_overflow, shamt_1_underflow, tempshift_1_overflow,
       tempshift_1_signout, tempshift_1_underflow, zerodetect_1_allzerosflag;
  wire [4:0] ExpoDiff_output;
  wire [9:0] n10bitmux_1_out_4, tempshift_1_expoout;
  wire [31:0] adder_1_out, n32bitmux_1_out, n32bitmux_2_out, n32bitmux_3_out, n32bitmux_4_out, negator_1_out,
       negator_2_out, resultnegate_1_negated, shamt_1_result, shifter_1_out, SigX_2_out_2, SigX_out_2,
       tempshift_1_sigout, zerodetect_1_outifallzeros;

  SignificandExtract SigX (.in_1(Input1), .out_2(SigX_out_2));
  SignificandExtract SigX_2 (.in_1(Input2), .out_2(SigX_2_out_2));
  _32bitMUX u_32bitmux_1 (.IN1(SigX_out_2), .IN2(SigX_2_out_2), .S(n7404_1__2__1y), .OUT(n32bitmux_1_out));
  _10bitMUX u_10bitmux_1 (
    .in_1(Input1[30:21]), .in_2(Input2[30:21]), .in_3(ExpoDiff_compare), .out_4(n10bitmux_1_out_4));
  _32bitMUX u_32bitmux_2 (.IN1(SigX_out_2), .IN2(SigX_2_out_2), .S(ExpoDiff_compare), .OUT(n32bitmux_2_out));
  ZeroDetect zerodetect_1 (
    .in_1(Input1), .in_2(Input2), .AllZerosFlag(zerodetect_1_allzerosflag),
    .OutIfAllZeros(zerodetect_1_outifallzeros));
  _7404 u_7404_1 (
    ._1__1A(ExpoDiff_compare), ._2__1Y(n7404_1__2__1y));  // open: _3__2A, _4__2Y, _5__3A, _6__3Y, _7__GND, _14__Vcc, _13__6A, _12__6Y, _11__5A, _10__5Y, _9__4A, _8__4Y
  Shifter #(.width(32), .shift("lr")) shifter_1 (.in(n32bitmux_1_out), .\dist (ExpoDiff_output), .out(shifter_1_out));
  _32bitMUX u_32bitmux_3 (.IN1(shifter_1_out), .IN2(negator_1_out), .S(n7432_1__11__4y), .OUT(n32bitmux_3_out));
  ExponentDifference ExpoDiff (
    .Expo1(Input1[30:21]), .Expo2(Input2[30:21]), .Output(ExpoDiff_output), .Compare(ExpoDiff_compare));  // open: VerySmall
  Negator #(.width(32)) negator_1 (.in(shifter_1_out), .out(negator_1_out));
  _32bitMUX u_32bitmux_4 (.IN1(n32bitmux_2_out), .IN2(negator_2_out), .S(n7432_1__3__1y), .OUT(n32bitmux_4_out));
  Adder #(.width(32)) adder_1 (.a(n32bitmux_3_out), .b(n32bitmux_4_out), .out(adder_1_out));  // open: cin, cout
  Negator #(.width(32)) negator_2 (.in(n32bitmux_2_out), .out(negator_2_out));
  ResultNegate resultnegate_1 (
    .in_1(adder_1_out), .SignedBit(resultnegate_1_signedbit), .Negated(resultnegate_1_negated));
  _7408 u_7408_1 (
    ._1__1A(Input2[31]), ._2__1B(ExpoDiff_compare), ._3__1Y(n7408_1__3__1y), ._4__2A(Input1[31]),
    ._5__2B(n7404_1__2__1y), ._6__2Y(n7408_1__6__2y), ._13__4B(n7404_1__2__1y), ._12__4A(Input2[31]),
    ._11__4Y(n7408_1__11__4y), ._10__3B(ExpoDiff_compare), ._9__3A(Input1[31]), ._8__3Y(n7408_1__8__3y));  // open: _7__GND, _14__Vcc
  _7432 u_7432_1 (
    ._1__1A(n7408_1__6__2y), ._2__1B(n7408_1__3__1y), ._3__1Y(n7432_1__3__1y), ._4__2A(tempshift_1_overflow),
    ._5__2B(shamt_1_overflow), ._6__2Y(n7432_1__6__2y), ._13__4B(n7408_1__8__3y), ._12__4A(n7408_1__11__4y),
    ._11__4Y(n7432_1__11__4y), ._10__3B(shamt_1_underflow), ._9__3A(tempshift_1_underflow),
    ._8__3Y(n7432_1__8__3y));  // open: _7__GND, _14__Vcc
  TempShift tempshift_1 (
    .Significand(resultnegate_1_negated), .Expo(n10bitmux_1_out_4), .Sign(resultnegate_1_signedbit),
    .SignOut(tempshift_1_signout), .SigOut(tempshift_1_sigout), .ExpoOut(tempshift_1_expoout),
    .UNDERFLOW(tempshift_1_underflow), .OVERFLOW(tempshift_1_overflow));
  _7408 u_7408_2 (
    ._1__1A(n7404_2__2__1y), ._2__1B(n7404_2__4__2y), ._3__1Y(n7408_2__3__1y), ._4__2A(n7408_2__3__1y),
    ._5__2B(shamt_1_overflow), ._6__2Y(n7408_2__6__2y), ._13__4B(n7408_2__3__1y),
    ._12__4A(shamt_1_underflow), ._11__4Y(n7408_2__11__4y));  // open: _7__GND, _14__Vcc, _10__3B, _9__3A, _8__3Y
  shamt shamt_1 (
    .Significand(tempshift_1_sigout), .Expo(tempshift_1_expoout), .Sign(tempshift_1_signout),
    .Result(shamt_1_result), .UNDERFLOW(shamt_1_underflow), .OVERFLOW(shamt_1_overflow));
  _7404 u_7404_2 (
    ._1__1A(tempshift_1_underflow), ._2__1Y(n7404_2__2__1y), ._3__2A(tempshift_1_overflow),
    ._4__2Y(n7404_2__4__2y));  // open: _5__3A, _6__3Y, _7__GND, _14__Vcc, _13__6A, _12__6Y, _11__5A, _10__5Y, _9__4A, _8__4Y
  _32bitMUX u_32bitmux_5 (
    .IN1(shamt_1_result), .IN2(zerodetect_1_outifallzeros), .S(zerodetect_1_allzerosflag), .OUT(Output));
  _74153 u_74153_1 (
    ._1__nG1(1'b0), ._2__B(zerodetect_1_allzerosflag), ._3__1C3(1'b0), ._6__1C0(n7432_1__8__3y),
    ._7__Y1(n74153_1__7__y1), ._15__nG2(1'b0), ._14__A(zerodetect_1_allzerosflag), ._13__2C3(1'b0),
    ._10__2C0(n7432_1__6__2y), ._9__Y2(n74153_1__9__y2));  // open: _4__1C2, _5__1C1, _8__GND, _16__Vcc, _12__2C2, _11__2C1
  _7432 u_7432_2 (
    ._1__1A(n7408_2__6__2y), ._2__1B(tempshift_1_overflow), ._3__1Y(Overflow), ._4__2A(n7408_2__11__4y),
    ._5__2B(tempshift_1_underflow), ._6__2Y(UnderFlow));  // open: _7__GND, _14__Vcc, _13__4B, _12__4A, _11__4Y, _10__3B, _9__3A, _8__3Y

  // Notes on the sheet:
  //   Right
  //   BigExpo
  //   ZeroDetect
  //   SmallIn
  //   BigIn
  //   ResultSign
endmodule

module SignificandExtract (
  input  [31:0] in_1,
  output [31:0] out_2
);

  wire [31:0] or_1_out, shifter_1_out, shifter_2_out;

  Shifter #(.width(32)) shifter_1 (.in(in_1), .\dist (5'b01011), .out(shifter_1_out));
  Shifter #(.width(32), .shift("lr")) shifter_2 (.in(shifter_1_out), .\dist (5'b00110), .out(shifter_2_out));
  assign or_1_out = shifter_2_out | 32'h4000000;  // OR_Gate or_1, 32 bits wide
  Shifter #(.width(32)) shifter_3 (.in(or_1_out), .\dist (5'b00011), .out(out_2));

  // Notes on the sheet:
  //   SignificandAdd
  //   GRS_shift
endmodule

module ExponentExtract (
  input  [7:0] in_1,
  output [7:0] out_2
);

  wire [7:0] shifter_1_out;

  Shifter shifter_1 (.in(in_1), .\dist (3'b001), .out(shifter_1_out));
  Shifter #(.shift("lr")) shifter_2 (.in(shifter_1_out), .\dist (3'b101), .out(out_2));
endmodule

module ExponentDifference (
  input  [9:0] Expo1,
  input  [9:0] Expo2,
  output [4:0] Output,
  output VerySmall,
  output Compare
);

  wire [9:0] n10bitmux_1_out_4, negator_1_out, subtractor_1_out;

  Subtractor #(.width(10)) subtractor_1 (.a(Expo1), .b(Expo2), .out(subtractor_1_out), .bout(Compare));  // open: bin
  Negator #(.width(10)) negator_1 (.in(subtractor_1_out), .out(negator_1_out));
  _10bitMUX u_10bitmux_1 (.in_1(subtractor_1_out), .in_2(negator_1_out), .in_3(Compare), .out_4(n10bitmux_1_out_4));
  _5bitMUX u_5bitmux_1 (.in_1(n10bitmux_1_out_4[4:0]), .in_2({5{1'b1}}), .S(VerySmall), .out_4(Output));
  Subtractor #(.width(5)) subtractor_2 (.a({5{1'b0}}), .b(n10bitmux_1_out_4[9:5]), .bout(VerySmall));  // open: out, bin
endmodule

module ResultNegate (
  input  [31:0] in_1,
  output SignedBit,
  output [31:0] Negated
);

  wire [31:0] negator_1_out;

  Negator #(.width(32)) negator_1 (.in(in_1), .out(negator_1_out));
  _32bitMUX u_32bitmux_1 (.IN1(in_1), .IN2(negator_1_out), .S(in_1[31]), .OUT(Negated));

  assign SignedBit = in_1[31];
endmodule

module shamt (
  input  [31:0] Significand,
  input  [9:0] Expo,
  input  Sign,
  output [31:0] Result,
  output UNDERFLOW,
  output OVERFLOW
);

  wire adder_1_cout, adder_2_cout, n7404_1__2__1y, n7408_1__3__1y, n7408_1__11__4y, n7432_1__3__1y,
       n7432_1__11__4y, priority_encoder_1_en_out, subtractor_1_bout, subtractor_2_bout, subtractor_3_bout;
  wire [4:0] n5bitmux_1_out_4, priority_encoder_1_out, subtractor_2_out;
  wire [9:0] adder_1_out, bit_extender_2_out, n10bitmux_1_out_4, subtractor_1_out;
  wire [31:0] adder_3_out, adder_4_out, bit_extender_1_out, bit_extender_3_out, n32bitmux_1_out,
       shifter_1_out, shifter_2_out, shifter_3_out, shifter_4_out, shifter_5_out, shifter_6_out;

  Priority_Encoder #(.select(5), .disabled(0)) priority_encoder_1 (
    .in0(Significand[0]), .in1(Significand[1]), .in2(Significand[2]), .in3(Significand[3]),
    .in4(Significand[4]), .in5(Significand[5]), .in6(Significand[6]), .in7(Significand[7]),
    .in8(Significand[8]), .in9(Significand[9]), .in10(Significand[10]), .in11(Significand[11]),
    .in12(Significand[12]), .in13(Significand[13]), .in14(Significand[14]), .in15(Significand[15]),
    .in16(Significand[16]), .in17(Significand[17]), .in18(Significand[18]), .in19(Significand[19]),
    .in20(Significand[20]), .in21(Significand[21]), .in22(Significand[22]), .in23(Significand[23]),
    .in24(Significand[24]), .in25(Significand[25]), .in26(Significand[26]), .in27(Significand[27]),
    .in28(Significand[28]), .in29(Significand[29]), .in30(Significand[30]), .in31(Significand[31]),
    .out(priority_encoder_1_out), .en_out(priority_encoder_1_en_out));  // open: gs, en_in
  assign bit_extender_1_out = {{31{1'b0}}, Sign};  // Bit_Extender bit_extender_1
  Shifter #(.width(32)) shifter_1 (.in(bit_extender_1_out), .\dist ({5{1'b1}}), .out(shifter_1_out));
  _5bitMUX u_5bitmux_1 (
    .in_1(priority_encoder_1_out), .in_2(5'b11101), .S(priority_encoder_1_en_out), .out_4(n5bitmux_1_out_4));
  Shifter #(.width(32)) shifter_2 (.in(Significand), .\dist (subtractor_2_out), .out(shifter_2_out));
  Shifter #(.width(32), .shift("lr")) shifter_3 (.in(Significand), .\dist (5'b00001), .out(shifter_3_out));
  Subtractor #(.width(10)) subtractor_1 (
    .a(Expo), .b(bit_extender_2_out), .out(subtractor_1_out), .bout(subtractor_1_bout));  // open: bin
  assign bit_extender_2_out = {{5{1'b0}}, subtractor_2_out};  // Bit_Extender bit_extender_2
  Subtractor #(.width(5)) subtractor_2 (
    .a(5'b11101), .b(n5bitmux_1_out_4), .out(subtractor_2_out), .bout(subtractor_2_bout));  // open: bin
  Subtractor #(.width(10)) subtractor_3 (.a(subtractor_1_out), .b(10'h1), .bout(subtractor_3_bout));  // open: out, bin
  Adder #(.width(10)) adder_1 (.a(Expo), .b(10'h1), .out(adder_1_out), .cout(adder_1_cout));  // open: cin
  Adder #(.width(10)) adder_2 (.a(Expo), .b(10'h2), .cout(adder_2_cout));  // open: out, cin
  _32bitMUX u_32bitmux_1 (.IN1(shifter_2_out), .IN2(shifter_3_out), .S(subtractor_2_bout), .OUT(n32bitmux_1_out));
  _10bitMUX u_10bitmux_1 (
    .in_1(subtractor_1_out), .in_2(adder_1_out), .in_3(subtractor_2_bout), .out_4(n10bitmux_1_out_4));
  _7404 u_7404_1 (
    ._1__1A(subtractor_2_bout), ._2__1Y(n7404_1__2__1y));  // open: _3__2A, _4__2Y, _5__3A, _6__3Y, _7__GND, _14__Vcc, _13__6A, _12__6Y, _11__5A, _10__5Y, _9__4A, _8__4Y
  _7408 u_7408_1 (
    ._1__1A(adder_2_cout), ._2__1B(subtractor_2_bout), ._3__1Y(n7408_1__3__1y), ._13__4B(n7404_1__2__1y),
    ._12__4A(subtractor_1_bout), ._11__4Y(n7408_1__11__4y));  // open: _4__2A, _5__2B, _6__2Y, _7__GND, _14__Vcc, _10__3B, _9__3A, _8__3Y
  Shifter #(.width(32)) shifter_4 (.in(n32bitmux_1_out), .\dist (5'b00011), .out(shifter_4_out));
  assign bit_extender_3_out = {{22{1'b0}}, n10bitmux_1_out_4};  // Bit_Extender bit_extender_3
  _7432 u_7432_1 (
    ._1__1A(n7408_1__3__1y), ._2__1B(adder_1_cout), ._3__1Y(n7432_1__3__1y), ._13__4B(n7408_1__11__4y),
    ._12__4A(subtractor_3_bout), ._11__4Y(n7432_1__11__4y));  // open: _4__2A, _5__2B, _6__2Y, _7__GND, _14__Vcc, _10__3B, _9__3A, _8__3Y
  _74153 u_74153_1 (
    ._1__nG1(1'b0), ._2__B(priority_encoder_1_en_out), ._3__1C3(1'b0), ._6__1C0(n7432_1__11__4y),
    ._7__Y1(UNDERFLOW), ._15__nG2(1'b0), ._14__A(priority_encoder_1_en_out), ._13__2C3(1'b0),
    ._10__2C0(n7432_1__3__1y), ._9__Y2(OVERFLOW));  // open: _4__1C2, _5__1C1, _8__GND, _16__Vcc, _12__2C2, _11__2C1
  Shifter #(.width(32)) shifter_5 (.in(bit_extender_3_out), .\dist (5'b10101), .out(shifter_5_out));
  Shifter #(.width(32), .shift("lr")) shifter_6 (.in(shifter_4_out), .\dist (5'b01011), .out(shifter_6_out));
  _32bitMUX u_32bitmux_2 (.IN1(adder_4_out), .IN2({32{1'b0}}), .S(priority_encoder_1_en_out), .OUT(Result));
  Adder #(.width(32)) adder_3 (.a(shifter_5_out), .b(shifter_1_out), .out(adder_3_out));  // open: cin, cout
  Adder #(.width(32)) adder_4 (.a(shifter_6_out), .b(adder_3_out), .out(adder_4_out));  // open: cin, cout

  // Notes on the sheet:
  //   Zero?
  //   Shamt
  //   ShamtBIG
endmodule

module TempShift (
  input  [31:0] Significand,
  input  [9:0] Expo,
  input  Sign,
  output [31:0] SigOut,
  output [9:0] ExpoOut,
  output SignOut,
  output UNDERFLOW,
  output OVERFLOW
);

  wire adder_1_cout, adder_2_cout, n7404_1__2__1y, n7404_1__4__2y, n7408_1__3__1y, n7408_1__11__4y,
       n7432_1__3__1y, n7432_1__6__2y, n7432_1__11__4y, priority_encoder_1_en_out, priority_encoder_2_gs,
       subtractor_1_bout, subtractor_2_bout, subtractor_3_bout;
  wire [4:0] priority_encoder_1_out, subtractor_2_out;
  wire [9:0] adder_1_out, bit_extender_1_out, n10bitmux_1_out_4, subtractor_1_out;
  wire [31:0] adder_3_out, adder_4_out, n32bitmux_1_out, n32bitmux_2_out, n32bitmux_3_out, shifter_1_out,
       shifter_2_out, shifter_3_out, shifter_4_out, shifter_5_out, shifter_6_out, shifter_7_out;

  Priority_Encoder #(.select(5), .disabled(0)) priority_encoder_1 (
    .in0(Significand[0]), .in1(Significand[1]), .in2(Significand[2]), .in3(Significand[3]),
    .in4(Significand[4]), .in5(Significand[5]), .in6(Significand[6]), .in7(Significand[7]),
    .in8(Significand[8]), .in9(Significand[9]), .in10(Significand[10]), .in11(Significand[11]),
    .in12(Significand[12]), .in13(Significand[13]), .in14(Significand[14]), .in15(Significand[15]),
    .in16(Significand[16]), .in17(Significand[17]), .in18(Significand[18]), .in19(Significand[19]),
    .in20(Significand[20]), .in21(Significand[21]), .in22(Significand[22]), .in23(Significand[23]),
    .in24(Significand[24]), .in25(Significand[25]), .in26(Significand[26]), .in27(Significand[27]),
    .in28(Significand[28]), .in29(Significand[29]), .in30(Significand[30]), .in31(Significand[31]),
    .out(priority_encoder_1_out), .en_out(priority_encoder_1_en_out));  // open: gs, en_in
  Shifter #(.width(32)) shifter_1 (.in(Significand), .\dist (subtractor_2_out), .out(shifter_1_out));
  Shifter #(.width(32), .shift("lr")) shifter_2 (.in(Significand), .\dist (5'b00001), .out(shifter_2_out));
  Subtractor #(.width(10)) subtractor_1 (
    .a(Expo), .b(bit_extender_1_out), .out(subtractor_1_out), .bout(subtractor_1_bout));  // open: bin
  Shifter #(.width(32), .shift("lr")) shifter_3 (.in(n32bitmux_1_out), .\dist (5'b01000), .out(shifter_3_out));
  assign bit_extender_1_out = {{5{1'b0}}, subtractor_2_out};  // Bit_Extender bit_extender_1
  Subtractor #(.width(5)) subtractor_2 (
    .a(5'b11101), .b(priority_encoder_1_out), .out(subtractor_2_out), .bout(subtractor_2_bout));  // open: bin
  Subtractor #(.width(10)) subtractor_3 (.a(subtractor_1_out), .b(10'h1), .bout(subtractor_3_bout));  // open: out, bin
  Adder #(.width(10)) adder_1 (.a(Expo), .b(10'h1), .out(adder_1_out), .cout(adder_1_cout));  // open: cin
  Adder #(.width(10)) adder_2 (.a(Expo), .b(10'h2), .cout(adder_2_cout));  // open: out, cin
  Shifter #(.width(32)) shifter_4 (.in(shifter_3_out), .\dist ({5{1'b1}}), .out(shifter_4_out));
  _32bitMUX u_32bitmux_1 (.IN1(shifter_1_out), .IN2(shifter_2_out), .S(subtractor_2_bout), .OUT(n32bitmux_1_out));
  _10bitMUX u_10bitmux_1 (
    .in_1(subtractor_1_out), .in_2(adder_1_out), .in_3(subtractor_2_bout), .out_4(n10bitmux_1_out_4));
  Shifter #(.width(32), .shift("lr")) shifter_5 (.in(shifter_4_out), .\dist (5'b10111), .out(shifter_5_out));
  Priority_Encoder priority_encoder_2 (
    .in0(n32bitmux_1_out[0]), .in1(n32bitmux_1_out[1]), .in2(n32bitmux_1_out[2]), .in3(n32bitmux_1_out[3]),
    .in4(n32bitmux_1_out[4]), .in5(n32bitmux_1_out[5]), .gs(priority_encoder_2_gs));  // open: in6, in7, out, en_in, en_out
  _7404 u_7404_1 (
    ._1__1A(n32bitmux_1_out[7]), ._2__1Y(n7404_1__2__1y), ._3__2A(subtractor_2_bout), ._4__2Y(n7404_1__4__2y));  // open: _5__3A, _6__3Y, _7__GND, _14__Vcc, _13__6A, _12__6Y, _11__5A, _10__5Y, _9__4A, _8__4Y
  _7408 u_7408_1 (
    ._1__1A(adder_2_cout), ._2__1B(subtractor_2_bout), ._3__1Y(n7408_1__3__1y), ._13__4B(subtractor_1_bout),
    ._12__4A(n7404_1__4__2y), ._11__4Y(n7408_1__11__4y));  // open: _4__2A, _5__2B, _6__2Y, _7__GND, _14__Vcc, _10__3B, _9__3A, _8__3Y
  Adder #(.width(32)) adder_3 (.a(shifter_5_out), .b(n32bitmux_1_out), .out(adder_3_out));  // open: cin, cout
  Adder #(.width(32)) adder_4 (.a(n32bitmux_1_out), .b(32'h80), .out(adder_4_out));  // open: cin, cout
  _7432 u_7432_1 (
    ._1__1A(n32bitmux_1_out[6]), ._2__1B(priority_encoder_2_gs), ._3__1Y(n7432_1__3__1y),
    ._4__2A(subtractor_3_bout), ._5__2B(n7408_1__11__4y), ._6__2Y(n7432_1__6__2y), ._13__4B(n7408_1__3__1y),
    ._12__4A(adder_1_cout), ._11__4Y(n7432_1__11__4y));  // open: _7__GND, _14__Vcc, _10__3B, _9__3A, _8__3Y
  _32bitMUX u_32bitmux_2 (.IN1(adder_3_out), .IN2(adder_4_out), .S(n7432_1__3__1y), .OUT(n32bitmux_2_out));
  _32bitMUX u_32bitmux_3 (.IN1(n32bitmux_2_out), .IN2(n32bitmux_1_out), .S(n7404_1__2__1y), .OUT(n32bitmux_3_out));
  _74153 u_74153_1 (
    ._1__nG1(1'b0), ._2__B(priority_encoder_1_en_out), ._3__1C3(1'b0), ._6__1C0(n7432_1__6__2y),
    ._7__Y1(UNDERFLOW), ._15__nG2(1'b0), ._14__A(priority_encoder_1_en_out), ._13__2C3(1'b0),
    ._10__2C0(n7432_1__11__4y), ._9__Y2(OVERFLOW));  // open: _4__1C2, _5__1C1, _8__GND, _16__Vcc, _12__2C2, _11__2C1
  Shifter #(.width(32), .shift("lr")) shifter_6 (.in(n32bitmux_3_out), .\dist (5'b01000), .out(shifter_6_out));
  _32bitMUX u_32bitmux_4 (.IN1(shifter_7_out), .IN2({32{1'b0}}), .S(priority_encoder_1_en_out), .OUT(SigOut));
  _10bitMUX u_10bitmux_2 (
    .in_1(n10bitmux_1_out_4), .in_2({10{1'b0}}), .in_3(priority_encoder_1_en_out), .out_4(ExpoOut));
  Shifter #(.width(32)) shifter_7 (.in(shifter_6_out), .\dist (5'b01000), .out(shifter_7_out));

  assign SignOut = Sign;

  // Notes on the sheet:
  //   Zero?
  //   ShamtBIG
  //   Shamt
  //   StickyBit
  //   Add last fraction bit with itself
  //   S OR R => RoundUp
  //   else Round even
  //   G=0, trunc
endmodule

module ZeroDetect (
  input  [31:0] in_1,
  input  [31:0] in_2,
  output AllZerosFlag,
  output [31:0] OutIfAllZeros
);

  wire priority_encoder_1_en_out, priority_encoder_2_en_out;
  wire [31:0] n32bitmux_1_out, shifter_1_out, shifter_2_out;

  Shifter #(.width(32)) shifter_1 (.in(in_1), .\dist (5'b00001), .out(shifter_1_out));
  Shifter #(.width(32)) shifter_2 (.in(in_2), .\dist (5'b00001), .out(shifter_2_out));
  Priority_Encoder #(.select(5), .disabled(0)) priority_encoder_1 (
    .in0(shifter_1_out[0]), .in1(shifter_1_out[1]), .in2(shifter_1_out[2]), .in3(shifter_1_out[3]),
    .in4(shifter_1_out[4]), .in5(shifter_1_out[5]), .in6(shifter_1_out[6]), .in7(shifter_1_out[7]),
    .in8(shifter_1_out[8]), .in9(shifter_1_out[9]), .in10(shifter_1_out[10]), .in11(shifter_1_out[11]),
    .in12(shifter_1_out[12]), .in13(shifter_1_out[13]), .in14(shifter_1_out[14]), .in15(shifter_1_out[15]),
    .in16(shifter_1_out[16]), .in17(shifter_1_out[17]), .in18(shifter_1_out[18]), .in19(shifter_1_out[19]),
    .in20(shifter_1_out[20]), .in21(shifter_1_out[21]), .in22(shifter_1_out[22]), .in23(shifter_1_out[23]),
    .in24(shifter_1_out[24]), .in25(shifter_1_out[25]), .in26(shifter_1_out[26]), .in27(shifter_1_out[27]),
    .in28(shifter_1_out[28]), .in29(shifter_1_out[29]), .in30(shifter_1_out[30]), .in31(shifter_1_out[31]),
    .en_out(priority_encoder_1_en_out));  // open: out, gs, en_in
  Priority_Encoder #(.select(5), .disabled(0)) priority_encoder_2 (
    .in0(shifter_2_out[0]), .in1(shifter_2_out[1]), .in2(shifter_2_out[2]), .in3(shifter_2_out[3]),
    .in4(shifter_2_out[4]), .in5(shifter_2_out[5]), .in6(shifter_2_out[6]), .in7(shifter_2_out[7]),
    .in8(shifter_2_out[8]), .in9(shifter_2_out[9]), .in10(shifter_2_out[10]), .in11(shifter_2_out[11]),
    .in12(shifter_2_out[12]), .in13(shifter_2_out[13]), .in14(shifter_2_out[14]), .in15(shifter_2_out[15]),
    .in16(shifter_2_out[16]), .in17(shifter_2_out[17]), .in18(shifter_2_out[18]), .in19(shifter_2_out[19]),
    .in20(shifter_2_out[20]), .in21(shifter_2_out[21]), .in22(shifter_2_out[22]), .in23(shifter_2_out[23]),
    .in24(shifter_2_out[24]), .in25(shifter_2_out[25]), .in26(shifter_2_out[26]), .in27(shifter_2_out[27]),
    .in28(shifter_2_out[28]), .in29(shifter_2_out[29]), .in30(shifter_2_out[30]), .in31(shifter_2_out[31]),
    .en_out(priority_encoder_2_en_out));  // open: out, gs, en_in
  _32bitMUX u_32bitmux_1 (.IN1(in_1), .IN2(in_2), .S(priority_encoder_1_en_out), .OUT(n32bitmux_1_out));
  _7432 u_7432_1 (
    ._1__1A(priority_encoder_1_en_out), ._2__1B(priority_encoder_2_en_out), ._3__1Y(AllZerosFlag));  // open: _4__2A, _5__2B, _6__2Y, _7__GND, _14__Vcc, _13__4B, _12__4A, _11__4Y, _10__3B, _9__3A, _8__3Y
  _32bitMUX u_32bitmux_2 (.IN1(in_2), .IN2(n32bitmux_1_out), .S(priority_encoder_2_en_out), .OUT(OutIfAllZeros));

  // Notes on the sheet:
  //   Exclude SignBit VV
endmodule

module _2bitMUX (
  input  [1:0] IN1,
  input  [1:0] IN2,
  input  S,
  output [1:0] Output
);

  _74157 u_74157_1 (
    ._1__S(S), ._2__A1(IN1[0]), ._3__B1(IN2[0]), ._4__Y1(Output[0]), ._5__A2(IN1[1]), ._6__B2(IN2[1]),
    ._7__Y2(Output[1]), ._15__G(1'b0));  // open: _8__GND, _16__Vcc, _14__A4, _13__B4, _12__Y4, _11__A3, _10__B3, _9__Y3
endmodule

module _4bitMUX (
  input  [3:0] IN1,
  input  [3:0] IN2,
  input  S,
  output [3:0] Out
);

  _2bitMUX u_2bitmux_1 (.IN1(IN1[1:0]), .IN2(IN2[1:0]), .S(S), .Output(Out[1:0]));
  _2bitMUX u_2bitmux_2 (.IN1(IN1[3:2]), .IN2(IN2[3:2]), .S(S), .Output(Out[3:2]));
endmodule

module _8bitMUX (
  input  [7:0] IN1,
  input  [7:0] IN2,
  input  S,
  output [7:0] Out
);

  _4bitMUX u_4bitmux_1 (.IN1(IN1[3:0]), .IN2(IN2[3:0]), .S(S), .Out(Out[3:0]));
  _4bitMUX u_4bitmux_2 (.IN1(IN1[7:4]), .IN2(IN2[7:4]), .S(S), .Out(Out[7:4]));
endmodule

module _16bitMUX (
  input  [15:0] IN1,
  input  [15:0] IN2,
  input  S,
  output [15:0] OUT
);

  _8bitMUX u_8bitmux_1 (.IN1(IN1[7:0]), .IN2(IN2[7:0]), .S(S), .Out(OUT[7:0]));
  _8bitMUX u_8bitmux_2 (.IN1(IN1[15:8]), .IN2(IN2[15:8]), .S(S), .Out(OUT[15:8]));
endmodule

module _32bitMUX (
  input  [31:0] IN1,
  input  [31:0] IN2,
  input  S,
  output [31:0] OUT
);

  _16bitMUX u_16bitmux_1 (.IN1(IN1[15:0]), .IN2(IN2[15:0]), .S(S), .OUT(OUT[15:0]));
  _16bitMUX u_16bitmux_2 (.IN1(IN1[31:16]), .IN2(IN2[31:16]), .S(S), .OUT(OUT[31:16]));
endmodule

module _10bitMUX (
  input  [9:0] in_1,
  input  [9:0] in_2,
  input  in_3,
  output [9:0] out_4
);

  _8bitMUX u_8bitmux_1 (.IN1(in_1[7:0]), .IN2(in_2[7:0]), .S(in_3), .Out(out_4[7:0]));
  _2bitMUX u_2bitmux_1 (.IN1(in_1[9:8]), .IN2(in_2[9:8]), .S(in_3), .Output(out_4[9:8]));
endmodule

module _5bitMUX (
  input  [4:0] in_1,
  input  [4:0] in_2,
  input  S,
  output [4:0] out_4
);

  _4bitMUX u_4bitmux_1 (.IN1(in_1[3:0]), .IN2(in_2[3:0]), .S(S), .Out(out_4[3:0]));
  _74157 u_74157_1 (
    ._1__S(S), ._2__A1(in_1[4]), ._3__B1(in_2[4]), ._4__Y1(out_4[4]), ._15__G(1'b0));  // open: _5__A2, _6__B2, _7__Y2, _8__GND, _16__Vcc, _14__A4, _13__B4, _12__Y4, _11__A3, _10__B3, _9__Y3
endmodule
