// Logisim project Trial8BitBigALUOK.circ as structural Verilog: 4 circuits, main circuit main
module main (
  input  [7:0] Input1,
  input  [7:0] Input2,
  output [7:0] out_3,
  output [7:0] out_4,
  output S1,
  output S2,
  output [2:0] out_7,
  output out_8,
  output [7:0] out_9,
  output [7:0] out_10
);

  wire and_1_out, and_2_out, and_3_out, and_4_out, not_1_out, or_1_out, or_2_out;
  wire [7:0] multiplexer_1_out, multiplexer_2_out, multiplexer_3_out, multiplexer_4_out, negator_1_out,
       negator_2_out, SigX_2_out_2, SigX_out_2;

  SignificandExtract SigX (.in_1(Input1), .out_2(SigX_out_2));
  SignificandExtract SigX_2 (.in_1(Input2), .out_2(SigX_2_out_2));
  Multiplexer #(.width(8), .enable("false")) multiplexer_1 (
    .in0(SigX_out_2), .in1(SigX_2_out_2), .out(multiplexer_1_out), .sel(not_1_out));
  Multiplexer #(.width(8), .enable("false")) multiplexer_2 (
    .in0(SigX_out_2), .in1(SigX_2_out_2), .out(multiplexer_2_out), .sel(out_8));
  SignificandExtract SigX_3 (.in_1(Input1), .out_2(out_3));
  SignificandExtract SigX_4 (.in_1(Input2), .out_2(out_4));
  not not_1 (not_1_out, out_8);
  Shifter #(.shift("lr")) shifter_1 (.in(multiplexer_1_out), .\dist (out_7), .out(out_9));
  Multiplexer #(.width(8), .enable("false")) multiplexer_3 (
    .in0(out_9), .in1(negator_1_out), .out(multiplexer_3_out), .sel(or_2_out));
  ExponentDifference ExpoDiff (.Expo1(Input1[6:4]), .Expo2(Input2[6:4]), .out_3(out_7), .Compare(out_8));
  Negator negator_1 (.in(out_9), .out(negator_1_out));
  Multiplexer #(.width(8), .enable("false")) multiplexer_4 (
    .in0(multiplexer_2_out), .in1(negator_2_out), .out(multiplexer_4_out), .sel(or_1_out));
  Adder adder_1 (.a(multiplexer_3_out), .b(multiplexer_4_out), .out(out_10));  // open: cin, cout
  Negator negator_2 (.in(multiplexer_2_out), .out(negator_2_out));
  and and_1 (and_1_out, not_1_out, Input1[7]);
  and and_2 (and_2_out, out_8, Input2[7]);
  or or_1 (or_1_out, and_1_out, and_2_out);
  and and_3 (and_3_out, not_1_out, Input2[7]);
  and and_4 (and_4_out, out_8, Input1[7]);
  or or_2 (or_2_out, and_3_out, and_4_out);

  assign S1 = Input1[7];
  assign S2 = Input2[7];

  // Notes on the sheet:
  //   Right
  //   SmallIn
  //   BigIn
endmodule

module SignificandExtract (
  input  [7:0] in_1,
  output [7:0] out_2
);

  wire [7:0] or_1_out, shifter_1_out, shifter_2_out;

  Shifter shifter_1 (.in(in_1), .\dist (3'b100), .out(shifter_1_out));
  Shifter #(.shift("lr")) shifter_2 (.in(shifter_1_out), .\dist (3'b100), .out(shifter_2_out));
  assign or_1_out = shifter_2_out | 8'h10;  // OR_Gate or_1, 8 bits wide
  Shifter shifter_3 (.in(or_1_out), .\dist (3'b011), .out(out_2));

  // Notes on the sheet:
  //   SignificandAdd
  //   GRS_shift
endmodule

module ExponentExtract (
  input  [7:0] in_1,
  output [7:0] out_2
);

  wire [7:0] shifter_1_out;

  Shifter shifter_1 (.in(in_1), .\dist (3'b001), .out(shifter_1_out));
  Shifter #(.shift("lr")) shifter_2 (.in(shifter_1_out), .\dist (3'b101), .out(out_2));
endmodule

module ExponentDifference (
  input  [2:0] Expo1,
  input  [2:0] Expo2,
  output [2:0] out_3,
  output Compare
);

  wire [2:0] negator_1_out, subtractor_1_out;

  Subtractor #(.width(3)) subtractor_1 (.a(Expo1), .b(Expo2), .out(subtractor_1_out), .bout(Compare));  // open: bin
  Negator #(.width(3)) negator_1 (.in(subtractor_1_out), .out(negator_1_out));
  Multiplexer #(.width(3), .enable("false")) multiplexer_1 (
    .in0(subtractor_1_out), .in1(negator_1_out), .out(out_3), .sel(Compare));
endmodule
