// Logisim project TrialB4Rounding.circ as structural Verilog: 6 circuits, main circuit main
module main (
  input  [31:0] Input1,
  input  [31:0] Input2,
  output [31:0] out_3,
  output [31:0] out_4,
  output S1,
  output S2,
  output [4:0] out_7,
  output out_8,
  output ResultSign,
  output [31:0] BigIn,
  output [31:0] out_11,
  output [31:0] out_12
);

  wire and_1_out, and_2_out, and_3_out, and_4_out, not_1_out, or_1_out, or_2_out;
  wire [9:0] multiplexer_2_out;
  wire [31:0] multiplexer_1_out, multiplexer_3_out, multiplexer_4_out, multiplexer_5_out, negator_1_out,
       negator_2_out, shifter_1_out, SigX_2_out_2, SigX_out_2;

  SignificandExtract SigX (.in_1(Input1), .out_2(SigX_out_2));
  SignificandExtract SigX_2 (.in_1(Input2), .out_2(SigX_2_out_2));
  Multiplexer #(.width(32), .enable("false")) multiplexer_1 (
    .in0(SigX_out_2), .in1(SigX_2_out_2), .out(multiplexer_1_out), .sel(not_1_out));
  Multiplexer #(.width(10), .enable("false")) multiplexer_2 (
    .in0(Input1[30:21]), .in1(Input2[30:21]), .out(multiplexer_2_out), .sel(out_8));
  Multiplexer #(.width(32), .enable("false")) multiplexer_3 (
    .in0(SigX_out_2), .in1(SigX_2_out_2), .out(multiplexer_3_out), .sel(out_8));
  SignificandExtract SigX_3 (.in_1(Input1), .out_2(out_3));
  SignificandExtract SigX_4 (.in_1(Input2), .out_2(out_4));
  not not_1 (not_1_out, out_8);
  Shifter #(.width(32), .shift("lr")) shifter_1 (.in(multiplexer_1_out), .\dist (out_7), .out(shifter_1_out));
  Multiplexer #(.width(32), .enable("false")) multiplexer_4 (
    .in0(shifter_1_out), .in1(negator_1_out), .out(multiplexer_4_out), .sel(or_2_out));
  ExponentDifference ExpoDiff (
    .Expo1(Input1[30:21]), .Expo2(Input2[30:21]), .Output(out_7), .Compare(out_8));  // open: Underflow
  Negator #(.width(32)) negator_1 (.in(shifter_1_out), .out(negator_1_out));
  Multiplexer #(.width(32), .enable("false")) multiplexer_5 (
    .in0(multiplexer_3_out), .in1(negator_2_out), .out(multiplexer_5_out), .sel(or_1_out));
  Adder #(.width(32)) adder_1 (.a(multiplexer_4_out), .b(multiplexer_5_out), .out(BigIn));  // open: cin, cout
  Negator #(.width(32)) negator_2 (.in(multiplexer_3_out), .out(negator_2_out));
  and and_1 (and_1_out, not_1_out, Input1[31]);
  ResultNegate resultnegate_1 (.in_1(BigIn), .SignedBit(ResultSign), .Negated(out_12));
  and and_2 (and_2_out, out_8, Input2[31]);
  or or_1 (or_1_out, and_1_out, and_2_out);
  shamt shamt_1 (
    .Significand(out_12), .Expo(multiplexer_2_out), .Sign(ResultSign), .Result(out_11));  // open: UNDERFLOW, OVERFLOW
  and and_3 (and_3_out, not_1_out, Input2[31]);
  and and_4 (and_4_out, out_8, Input1[31]);
  or or_2 (or_2_out, and_3_out, and_4_out);

  assign S1 = Input1[31];
  assign S2 = Input2[31];

  // Notes on the sheet:
  //   Right
  //   BigExpo
  //   SmallIn
endmodule

module SignificandExtract (
  input  [31:0] in_1,
  output [31:0] out_2
);

  wire [31:0] or_1_out, shifter_1_out, shifter_2_out;

  Shifter #(.width(32)) shifter_1 (.in(in_1), .\dist (5'b01011), .out(shifter_1_out));
  Shifter #(.width(32), .shift("lr")) shifter_2 (.in(shifter_1_out), .\dist (5'b00110), .out(shifter_2_out));
  assign or_1_out = shifter_2_out | 32'h4000000;  // OR_Gate or_1, 32 bits wide
  Shifter #(.width(32)) shifter_3 (.in(or_1_out), .\dist (5'b00011), .out(out_2));

  // Notes on the sheet:
  //   SignificandAdd
  //   GRS_shift
endmodule

module ExponentExtract (
  input  [7:0] in_1,
  output [7:0] out_2
);

  wire [7:0] shifter_1_out;

  Shifter shifter_1 (.in(in_1), .\dist (3'b001), .out(shifter_1_out));
  Shifter #(.shift("lr")) shifter_2 (.in(shifter_1_out), .\dist (3'b101), .out(out_2));
endmodule

module ExponentDifference (
  input  [9:0] Expo1,
  input  [9:0] Expo2,
  output [4:0] Output,
  output Underflow,
  output Compare
);

  wire [9:0] multiplexer_1_out, negator_1_out, subtractor_1_out;

  Subtractor #(.width(10)) subtractor_1 (.a(Expo1), .b(Expo2), .out(subtractor_1_out), .bout(Compare));  // open: bin
  Negator #(.width(10)) negator_1 (.in(subtractor_1_out), .out(negator_1_out));
  Multiplexer #(.width(10), .enable("false")) multiplexer_1 (
    .in0(subtractor_1_out), .in1(negator_1_out), .out(multiplexer_1_out), .sel(Compare));
  Multiplexer #(.width(5), .enable("false")) multiplexer_2 (
    .in0(multiplexer_1_out[4:0]), .in1({5{1'b1}}), .out(Output), .sel(Underflow));
  Subtractor #(.width(5)) subtractor_2 (.a({5{1'b0}}), .b(multiplexer_1_out[9:5]), .bout(Underflow));  // open: out, bin
endmodule

module ResultNegate (
  input  [31:0] in_1,
  output SignedBit,
  output [31:0] Negated
);

  wire [31:0] negator_1_out;

  Negator #(.width(32)) negator_1 (.in(in_1), .out(negator_1_out));
  Multiplexer #(.width(32), .enable("false")) multiplexer_1 (
    .in0(in_1), .in1(negator_1_out), .out(Negated), .sel(in_1[31]));

  assign SignedBit = in_1[31];
endmodule

module shamt (
  input  [31:0] Significand,
  input  [9:0] Expo,
  input  Sign,
  output [31:0] Result,
  output UNDERFLOW,
  output OVERFLOW
);

  wire adder_1_cout, subtractor_2_bout;
  wire [4:0] priority_encoder_1_out, subtractor_2_out;
  wire [9:0] adder_1_out, bit_extender_2_out, multiplexer_2_out, subtractor_1_out;
  wire [31:0] adder_2_out, bit_extender_1_out, bit_extender_3_out, multiplexer_1_out, shifter_1_out,
       shifter_2_out, shifter_3_out, shifter_4_out, shifter_5_out, shifter_6_out;

  Priority_Encoder #(.select(5)) priority_encoder_1 (
    .in0(Significand[0]), .in1(Significand[1]), .in2(Significand[2]), .in3(Significand[3]),
    .in4(Significand[4]), .in5(Significand[5]), .in6(Significand[6]), .in7(Significand[7]),
    .in8(Significand[8]), .in9(Significand[9]), .in10(Significand[10]), .in11(Significand[11]),
    .in12(Significand[12]), .in13(Significand[13]), .in14(Significand[14]), .in15(Significand[15]),
    .in16(Significand[16]), .in17(Significand[17]), .in18(Significand[18]), .in19(Significand[19]),
    .in20(Significand[20]), .in21(Significand[21]), .in22(Significand[22]), .in23(Significand[23]),
    .in24(Significand[24]), .in25(Significand[25]), .in26(Significand[26]), .in27(Significand[27]),
    .in28(Significand[28]), .in29(Significand[29]), .in30(Significand[30]), .in31(Significand[31]),
    .out(priority_encoder_1_out));  // open: gs, en_out, en_in
  assign bit_extender_1_out = {{31{1'b0}}, Sign};  // Bit_Extender bit_extender_1
  Shifter #(.width(32)) shifter_1 (.in(bit_extender_1_out), .\dist ({5{1'b1}}), .out(shifter_1_out));
  Shifter #(.width(32)) shifter_2 (.in(Significand), .\dist (subtractor_2_out), .out(shifter_2_out));
  Shifter #(.width(32), .shift("lr")) shifter_3 (.in(Significand), .\dist (5'b00001), .out(shifter_3_out));
  Subtractor #(.width(10)) subtractor_1 (
    .a(Expo), .b(bit_extender_2_out), .out(subtractor_1_out), .bout(UNDERFLOW));  // open: bin
  assign bit_extender_2_out = {{5{1'b0}}, subtractor_2_out};  // Bit_Extender bit_extender_2
  Subtractor #(.width(5)) subtractor_2 (
    .a(5'b11101), .b(priority_encoder_1_out), .out(subtractor_2_out), .bout(subtractor_2_bout));  // open: bin
  Adder #(.width(10)) adder_1 (.a(Expo), .b(10'h1), .out(adder_1_out), .cout(adder_1_cout));  // open: cin
  Multiplexer #(.width(32), .enable("false")) multiplexer_1 (
    .in0(shifter_2_out), .in1(shifter_3_out), .out(multiplexer_1_out), .sel(subtractor_2_bout));
  Multiplexer #(.width(10), .enable("false")) multiplexer_2 (
    .in0(subtractor_1_out), .in1(adder_1_out), .out(multiplexer_2_out), .sel(subtractor_2_bout));
  _7408 u_7408_1 (
    ._1__1A(adder_1_cout), ._2__1B(subtractor_2_bout), ._3__1Y(OVERFLOW));  // open: _4__2A, _5__2B, _6__2Y, _7__GND, _14__Vcc, _13__4B, _12__4A, _11__4Y, _10__3B, _9__3A, _8__3Y
  Shifter #(.width(32)) shifter_4 (.in(multiplexer_1_out), .\dist (5'b00011), .out(shifter_4_out));
  assign bit_extender_3_out = {{22{1'b0}}, multiplexer_2_out};  // Bit_Extender bit_extender_3
  Shifter #(.width(32)) shifter_5 (.in(bit_extender_3_out), .\dist (5'b10101), .out(shifter_5_out));
  Shifter #(.width(32), .shift("lr")) shifter_6 (.in(shifter_4_out), .\dist (5'b01011), .out(shifter_6_out));
  Adder #(.width(32)) adder_2 (.a(shifter_5_out), .b(shifter_1_out), .out(adder_2_out));  // open: cin, cout
  Adder #(.width(32)) adder_3 (.a(shifter_6_out), .b(adder_2_out), .out(Result));  // open: cin, cout

  // Notes on the sheet:
  //   Shamt
  //   ShamtBIG
  //   Round
endmodule
