// Logisim project TrialB4Zero2.circ as structural Verilog: 7 circuits, main circuit main
module main (
  input  [31:0] Input1,
  input  [31:0] Input2,
  output [31:0] out_3,
  output [31:0] out_4,
  output S1,
  output S2,
  output [4:0] out_7,
  output out_8,
  output UnderFlow,
  output Overflow,
  output ResultSign,
  output [31:0] BigIn,
  output [31:0] out_13,
  output [31:0] out_14
);

  wire n7404_1__2__1y, n7408_1__3__1y, n7408_1__6__2y, n7408_1__8__3y, n7408_1__11__4y, n7432_1__3__1y,
       n7432_1__11__4y, shamt_1_overflow, shamt_1_underflow, tempshift_1_overflow, tempshift_1_signout,
       tempshift_1_underflow;
  wire [9:0] multiplexer_2_out, tempshift_1_expoout;
  wire [31:0] multiplexer_1_out, multiplexer_3_out, multiplexer_4_out, multiplexer_5_out, negator_1_out,
       negator_2_out, shifter_1_out, SigX_2_out_2, SigX_out_2, tempshift_1_sigout;

  SignificandExtract SigX (.in_1(Input1), .out_2(SigX_out_2));
  SignificandExtract SigX_2 (.in_1(Input2), .out_2(SigX_2_out_2));
  Multiplexer #(.width(32), .enable("false")) multiplexer_1 (
    .in0(SigX_out_2), .in1(SigX_2_out_2), .out(multiplexer_1_out), .sel(n7404_1__2__1y));
  Multiplexer #(.width(10), .enable("false")) multiplexer_2 (
    .in0(Input1[30:21]), .in1(Input2[30:21]), .out(multiplexer_2_out), .sel(out_8));
  Multiplexer #(.width(32), .enable("false")) multiplexer_3 (
    .in0(SigX_out_2), .in1(SigX_2_out_2), .out(multiplexer_3_out), .sel(out_8));
  SignificandExtract SigX_3 (.in_1(Input1), .out_2(out_3));
  SignificandExtract SigX_4 (.in_1(Input2), .out_2(out_4));
  _7404 u_7404_1 (
    ._1__1A(out_8), ._2__1Y(n7404_1__2__1y));  // open: _3__2A, _4__2Y, _5__3A, _6__3Y, _7__GND, _14__Vcc, _13__6A, _12__6Y, _11__5A, _10__5Y, _9__4A, _8__4Y
  Shifter #(.width(32), .shift("lr")) shifter_1 (.in(multiplexer_1_out), .\dist (out_7), .out(shifter_1_out));
  Multiplexer #(.width(32), .enable("false")) multiplexer_4 (
    .in0(shifter_1_out), .in1(negator_1_out), .out(multiplexer_4_out), .sel(n7432_1__11__4y));
  ExponentDifference ExpoDiff (
    .Expo1(Input1[30:21]), .Expo2(Input2[30:21]), .Output(out_7), .Compare(out_8));  // open: VerySmall
  Negator #(.width(32)) negator_1 (.in(shifter_1_out), .out(negator_1_out));
  Multiplexer #(.width(32), .enable("false")) multiplexer_5 (
    .in0(multiplexer_3_out), .in1(negator_2_out), .out(multiplexer_5_out), .sel(n7432_1__3__1y));
  Adder #(.width(32)) adder_1 (.a(multiplexer_4_out), .b(multiplexer_5_out), .out(BigIn));  // open: cin, cout
  Negator #(.width(32)) negator_2 (.in(multiplexer_3_out), .out(negator_2_out));
  ResultNegate resultnegate_1 (.in_1(BigIn), .SignedBit(ResultSign), .Negated(out_14));
  _7408 u_7408_1 (
    ._1__1A(Input2[31]), ._2__1B(out_8), ._3__1Y(n7408_1__3__1y), ._4__2A(Input1[31]),
    ._5__2B(n7404_1__2__1y), ._6__2Y(n7408_1__6__2y), ._13__4B(n7404_1__2__1y), ._12__4A(Input2[31]),
    ._11__4Y(n7408_1__11__4y), ._10__3B(out_8), ._9__3A(Input1[31]), ._8__3Y(n7408_1__8__3y));  // open: _7__GND, _14__Vcc
  _7432 u_7432_1 (
    ._1__1A(n7408_1__6__2y), ._2__1B(n7408_1__3__1y), ._3__1Y(n7432_1__3__1y), ._4__2A(tempshift_1_overflow),
    ._5__2B(shamt_1_overflow), ._6__2Y(Overflow), ._13__4B(n7408_1__8__3y), ._12__4A(n7408_1__11__4y),
    ._11__4Y(n7432_1__11__4y), ._10__3B(shamt_1_underflow), ._9__3A(tempshift_1_underflow), ._8__3Y(UnderFlow));  // open: _7__GND, _14__Vcc
  TempShift tempshift_1 (
    .Significand(out_14), .Expo(multiplexer_2_out), .Sign(ResultSign), .SignOut(tempshift_1_signout),
    .SigOut(tempshift_1_sigout), .ExpoOut(tempshift_1_expoout), .UNDERFLOW(tempshift_1_underflow),
    .OVERFLOW(tempshift_1_overflow));
  shamt shamt_1 (
    .Significand(tempshift_1_sigout), .Expo(tempshift_1_expoout), .Sign(tempshift_1_signout),
    .Result(out_13), .UNDERFLOW(shamt_1_underflow), .OVERFLOW(shamt_1_overflow));

  assign S1 = Input1[31];
  assign S2 = Input2[31];

  // Notes on the sheet:
  //   Right
  //   BigExpo
  //   SmallIn
endmodule

module SignificandExtract (
  input  [31:0] in_1,
  output [31:0] out_2
);

  wire [31:0] or_1_out, shifter_1_out, shifter_2_out;

  Shifter #(.width(32)) shifter_1 (.in(in_1), .\dist (5'b01011), .out(shifter_1_out));
  Shifter #(.width(32), .shift("lr")) shifter_2 (.in(shifter_1_out), .\dist (5'b00110), .out(shifter_2_out));
  assign or_1_out = shifter_2_out | 32'h4000000;  // OR_Gate or_1, 32 bits wide
  Shifter #(.width(32)) shifter_3 (.in(or_1_out), .\dist (5'b00011), .out(out_2));

  // Notes on the sheet:
  //   SignificandAdd
  //   GRS_shift
endmodule

module ExponentExtract (
  input  [7:0] in_1,
  output [7:0] out_2
);

  wire [7:0] shifter_1_out;

  Shifter shifter_1 (.in(in_1), .\dist (3'b001), .out(shifter_1_out));
  Shifter #(.shift("lr")) shifter_2 (.in(shifter_1_out), .\dist (3'b101), .out(out_2));
endmodule

module ExponentDifference (
  input  [9:0] Expo1,
  input  [9:0] Expo2,
  output [4:0] Output,
  output VerySmall,
  output Compare
);

  wire [9:0] multiplexer_1_out, negator_1_out, subtractor_1_out;

  Subtractor #(.width(10)) subtractor_1 (.a(Expo1), .b(Expo2), .out(subtractor_1_out), .bout(Compare));  // open: bin
  Negator #(.width(10)) negator_1 (.in(subtractor_1_out), .out(negator_1_out));
  Multiplexer #(.width(10), .enable("false")) multiplexer_1 (
    .in0(subtractor_1_out), .in1(negator_1_out), .out(multiplexer_1_out), .sel(Compare));
  Multiplexer #(.width(5), .enable("false")) multiplexer_2 (
    .in0(multiplexer_1_out[4:0]), .in1({5{1'b1}}), .out(Output), .sel(VerySmall));
  Subtractor #(.width(5)) subtractor_2 (.a({5{1'b0}}), .b(multiplexer_1_out[9:5]), .bout(VerySmall));  // open: out, bin
endmodule

module ResultNegate (
  input  [31:0] in_1,
  output SignedBit,
  output [31:0] Negated
);

  wire [31:0] negator_1_out;

  Negator #(.width(32)) negator_1 (.in(in_1), .out(negator_1_out));
  Multiplexer #(.width(32), .enable("false")) multiplexer_1 (
    .in0(in_1), .in1(negator_1_out), .out(Negated), .sel(in_1[31]));

  assign SignedBit = in_1[31];
endmodule

module shamt (
  input  [31:0] Significand,
  input  [9:0] Expo,
  input  Sign,
  output [31:0] Result,
  output UNDERFLOW,
  output OVERFLOW
);

  wire adder_1_cout, adder_2_cout, n7408_1__3__1y, n7432_1__3__1y, priority_encoder_1_en_out,
       subtractor_1_bout, subtractor_2_bout;
  wire [4:0] multiplexer_1_out, priority_encoder_1_out, subtractor_2_out;
  wire [9:0] adder_1_out, bit_extender_2_out, multiplexer_3_out, subtractor_1_out;
  wire [31:0] adder_3_out, adder_4_out, bit_extender_1_out, bit_extender_3_out, multiplexer_2_out,
       shifter_1_out, shifter_2_out, shifter_3_out, shifter_4_out, shifter_5_out, shifter_6_out;

  Priority_Encoder #(.select(5), .disabled(0)) priority_encoder_1 (
    .in0(Significand[0]), .in1(Significand[1]), .in2(Significand[2]), .in3(Significand[3]),
    .in4(Significand[4]), .in5(Significand[5]), .in6(Significand[6]), .in7(Significand[7]),
    .in8(Significand[8]), .in9(Significand[9]), .in10(Significand[10]), .in11(Significand[11]),
    .in12(Significand[12]), .in13(Significand[13]), .in14(Significand[14]), .in15(Significand[15]),
    .in16(Significand[16]), .in17(Significand[17]), .in18(Significand[18]), .in19(Significand[19]),
    .in20(Significand[20]), .in21(Significand[21]), .in22(Significand[22]), .in23(Significand[23]),
    .in24(Significand[24]), .in25(Significand[25]), .in26(Significand[26]), .in27(Significand[27]),
    .in28(Significand[28]), .in29(Significand[29]), .in30(Significand[30]), .in31(Significand[31]),
    .out(priority_encoder_1_out), .en_out(priority_encoder_1_en_out));  // open: gs, en_in
  assign bit_extender_1_out = {{31{1'b0}}, Sign};  // Bit_Extender bit_extender_1
  Shifter #(.width(32)) shifter_1 (.in(bit_extender_1_out), .\dist ({5{1'b1}}), .out(shifter_1_out));
  Multiplexer #(.width(5), .enable("false")) multiplexer_1 (
    .in0(priority_encoder_1_out), .in1(5'b11101), .out(multiplexer_1_out), .sel(priority_encoder_1_en_out));
  Shifter #(.width(32)) shifter_2 (.in(Significand), .\dist (subtractor_2_out), .out(shifter_2_out));
  Shifter #(.width(32), .shift("lr")) shifter_3 (.in(Significand), .\dist (5'b00001), .out(shifter_3_out));
  Subtractor #(.width(10)) subtractor_1 (
    .a(Expo), .b(bit_extender_2_out), .out(subtractor_1_out), .bout(subtractor_1_bout));  // open: bin
  assign bit_extender_2_out = {{5{1'b0}}, subtractor_2_out};  // Bit_Extender bit_extender_2
  Subtractor #(.width(5)) subtractor_2 (
    .a(5'b11101), .b(multiplexer_1_out), .out(subtractor_2_out), .bout(subtractor_2_bout));  // open: bin
  Adder #(.width(10)) adder_1 (.a(Expo), .b(10'h1), .out(adder_1_out), .cout(adder_1_cout));  // open: cin
  Adder #(.width(10)) adder_2 (.a(Expo), .b(10'h2), .cout(adder_2_cout));  // open: out, cin
  Multiplexer #(.width(32), .enable("false")) multiplexer_2 (
    .in0(shifter_2_out), .in1(shifter_3_out), .out(multiplexer_2_out), .sel(subtractor_2_bout));
  Multiplexer #(.width(10), .enable("false")) multiplexer_3 (
    .in0(subtractor_1_out), .in1(adder_1_out), .out(multiplexer_3_out), .sel(subtractor_2_bout));
  _7408 u_7408_1 (
    ._1__1A(adder_2_cout), ._2__1B(subtractor_2_bout), ._3__1Y(n7408_1__3__1y));  // open: _4__2A, _5__2B, _6__2Y, _7__GND, _14__Vcc, _13__4B, _12__4A, _11__4Y, _10__3B, _9__3A, _8__3Y
  Shifter #(.width(32)) shifter_4 (.in(multiplexer_2_out), .\dist (5'b00011), .out(shifter_4_out));
  assign bit_extender_3_out = {{22{1'b0}}, multiplexer_3_out};  // Bit_Extender bit_extender_3
  _7432 u_7432_1 (
    ._1__1A(n7408_1__3__1y), ._2__1B(adder_1_cout), ._3__1Y(n7432_1__3__1y));  // open: _4__2A, _5__2B, _6__2Y, _7__GND, _14__Vcc, _13__4B, _12__4A, _11__4Y, _10__3B, _9__3A, _8__3Y
  _74153 u_74153_1 (
    ._1__nG1(1'b0), ._2__B(priority_encoder_1_en_out), ._3__1C3(1'b0), ._6__1C0(subtractor_1_bout),
    ._7__Y1(UNDERFLOW), ._15__nG2(1'b0), ._14__A(priority_encoder_1_en_out), ._13__2C3(1'b0),
    ._10__2C0(n7432_1__3__1y), ._9__Y2(OVERFLOW));  // open: _4__1C2, _5__1C1, _8__GND, _16__Vcc, _12__2C2, _11__2C1
  Shifter #(.width(32)) shifter_5 (.in(bit_extender_3_out), .\dist (5'b10101), .out(shifter_5_out));
  Shifter #(.width(32), .shift("lr")) shifter_6 (.in(shifter_4_out), .\dist (5'b01011), .out(shifter_6_out));
  Multiplexer #(.width(32), .enable("false")) multiplexer_4 (
    .in0(adder_4_out), .in1({32{1'b0}}), .out(Result), .sel(priority_encoder_1_en_out));
  Adder #(.width(32)) adder_3 (.a(shifter_5_out), .b(shifter_1_out), .out(adder_3_out));  // open: cin, cout
  Adder #(.width(32)) adder_4 (.a(shifter_6_out), .b(adder_3_out), .out(adder_4_out));  // open: cin, cout

  // Notes on the sheet:
  //   Zero?
  //   Shamt
  //   ShamtBIG
endmodule

module TempShift (
  input  [31:0] Significand,
  input  [9:0] Expo,
  input  Sign,
  output [31:0] SigOut,
  output [9:0] ExpoOut,
  output SignOut,
  output UNDERFLOW,
  output OVERFLOW
);

  wire adder_1_cout, adder_2_cout, n7404_1__2__1y, n7408_1__3__1y, n7432_1__3__1y, n7432_1__11__4y,
       priority_encoder_1_en_out, priority_encoder_2_gs, subtractor_1_bout, subtractor_2_bout;
  wire [4:0] priority_encoder_1_out, subtractor_2_out;
  wire [9:0] adder_1_out, bit_extender_1_out, multiplexer_2_out, subtractor_1_out;
  wire [31:0] adder_3_out, adder_4_out, multiplexer_1_out, multiplexer_3_out, multiplexer_4_out,
       shifter_1_out, shifter_2_out, shifter_3_out, shifter_4_out, shifter_5_out, shifter_6_out,
       shifter_7_out;

  Priority_Encoder #(.select(5), .disabled(0)) priority_encoder_1 (
    .in0(Significand[0]), .in1(Significand[1]), .in2(Significand[2]), .in3(Significand[3]),
    .in4(Significand[4]), .in5(Significand[5]), .in6(Significand[6]), .in7(Significand[7]),
    .in8(Significand[8]), .in9(Significand[9]), .in10(Significand[10]), .in11(Significand[11]),
    .in12(Significand[12]), .in13(Significand[13]), .in14(Significand[14]), .in15(Significand[15]),
    .in16(Significand[16]), .in17(Significand[17]), .in18(Significand[18]), .in19(Significand[19]),
    .in20(Significand[20]), .in21(Significand[21]), .in22(Significand[22]), .in23(Significand[23]),
    .in24(Significand[24]), .in25(Significand[25]), .in26(Significand[26]), .in27(Significand[27]),
    .in28(Significand[28]), .in29(Significand[29]), .in30(Significand[30]), .in31(Significand[31]),
    .out(priority_encoder_1_out), .en_out(priority_encoder_1_en_out));  // open: gs, en_in
  Shifter #(.width(32)) shifter_1 (.in(Significand), .\dist (subtractor_2_out), .out(shifter_1_out));
  Shifter #(.width(32), .shift("lr")) shifter_2 (.in(Significand), .\dist (5'b00001), .out(shifter_2_out));
  Subtractor #(.width(10)) subtractor_1 (
    .a(Expo), .b(bit_extender_1_out), .out(subtractor_1_out), .bout(subtractor_1_bout));  // open: bin
  Shifter #(.width(32), .shift("lr")) shifter_3 (.in(multiplexer_1_out), .\dist (5'b01000), .out(shifter_3_out));
  assign bit_extender_1_out = {{5{1'b0}}, subtractor_2_out};  // Bit_Extender bit_extender_1
  Subtractor #(.width(5)) subtractor_2 (
    .a(5'b11101), .b(priority_encoder_1_out), .out(subtractor_2_out), .bout(subtractor_2_bout));  // open: bin
  Adder #(.width(10)) adder_1 (.a(Expo), .b(10'h1), .out(adder_1_out), .cout(adder_1_cout));  // open: cin
  Adder #(.width(10)) adder_2 (.a(Expo), .b(10'h2), .cout(adder_2_cout));  // open: out, cin
  Shifter #(.width(32)) shifter_4 (.in(shifter_3_out), .\dist ({5{1'b1}}), .out(shifter_4_out));
  Multiplexer #(.width(32), .enable("false")) multiplexer_1 (
    .in0(shifter_1_out), .in1(shifter_2_out), .out(multiplexer_1_out), .sel(subtractor_2_bout));
  Multiplexer #(.width(10), .enable("false")) multiplexer_2 (
    .in0(subtractor_1_out), .in1(adder_1_out), .out(multiplexer_2_out), .sel(subtractor_2_bout));
  Shifter #(.width(32), .shift("lr")) shifter_5 (.in(shifter_4_out), .\dist (5'b10111), .out(shifter_5_out));
  Priority_Encoder priority_encoder_2 (
    .in0(multiplexer_1_out[0]), .in1(multiplexer_1_out[1]), .in2(multiplexer_1_out[2]),
    .in3(multiplexer_1_out[3]), .in4(multiplexer_1_out[4]), .in5(multiplexer_1_out[5]),
    .gs(priority_encoder_2_gs));  // open: in6, in7, out, en_in, en_out
  _7404 u_7404_1 (
    ._1__1A(multiplexer_1_out[7]), ._2__1Y(n7404_1__2__1y));  // open: _3__2A, _4__2Y, _5__3A, _6__3Y, _7__GND, _14__Vcc, _13__6A, _12__6Y, _11__5A, _10__5Y, _9__4A, _8__4Y
  _7408 u_7408_1 (
    ._1__1A(adder_2_cout), ._2__1B(subtractor_2_bout), ._3__1Y(n7408_1__3__1y));  // open: _4__2A, _5__2B, _6__2Y, _7__GND, _14__Vcc, _13__4B, _12__4A, _11__4Y, _10__3B, _9__3A, _8__3Y
  Adder #(.width(32)) adder_3 (.a(shifter_5_out), .b(multiplexer_1_out), .out(adder_3_out));  // open: cin, cout
  Adder #(.width(32)) adder_4 (.a(multiplexer_1_out), .b(32'h80), .out(adder_4_out));  // open: cin, cout
  _7432 u_7432_1 (
    ._1__1A(multiplexer_1_out[6]), ._2__1B(priority_encoder_2_gs), ._3__1Y(n7432_1__3__1y),
    ._13__4B(n7408_1__3__1y), ._12__4A(adder_1_cout), ._11__4Y(n7432_1__11__4y));  // open: _4__2A, _5__2B, _6__2Y, _7__GND, _14__Vcc, _10__3B, _9__3A, _8__3Y
  Multiplexer #(.width(32), .enable("false")) multiplexer_3 (
    .in0(adder_3_out), .in1(adder_4_out), .out(multiplexer_3_out), .sel(n7432_1__3__1y));
  Multiplexer #(.width(32), .enable("false")) multiplexer_4 (
    .in0(multiplexer_3_out), .in1(multiplexer_1_out), .out(multiplexer_4_out), .sel(n7404_1__2__1y));
  _74153 u_74153_1 (
    ._1__nG1(1'b0), ._2__B(priority_encoder_1_en_out), ._3__1C3(1'b0), ._6__1C0(subtractor_1_bout),
    ._7__Y1(UNDERFLOW), ._15__nG2(1'b0), ._14__A(priority_encoder_1_en_out), ._13__2C3(1'b0),
    ._10__2C0(n7432_1__11__4y), ._9__Y2(OVERFLOW));  // open: _4__1C2, _5__1C1, _8__GND, _16__Vcc, _12__2C2, _11__2C1
  Shifter #(.width(32), .shift("lr")) shifter_6 (.in(multiplexer_4_out), .\dist (5'b01000), .out(shifter_6_out));
  Multiplexer #(.width(32), .enable("false")) multiplexer_5 (
    .in0(shifter_7_out), .in1({32{1'b0}}), .out(SigOut), .sel(priority_encoder_1_en_out));
  Multiplexer #(.width(10), .enable("false")) multiplexer_6 (
    .in0(multiplexer_2_out), .in1({10{1'b0}}), .out(ExpoOut), .sel(priority_encoder_1_en_out));
  Shifter #(.width(32)) shifter_7 (.in(shifter_6_out), .\dist (5'b01000), .out(shifter_7_out));

  assign SignOut = Sign;

  // Notes on the sheet:
  //   Zero?
  //   ShamtBIG
  //   Shamt
  //   StickyBit
  //   Add last fraction bit with itself
  //   S OR R => RoundUp
  //   else Round even
  //   G=0, trunc
endmodule
