// Logisim project A1_G3.circ as structural Verilog: 6 circuits, main circuit main
module main (
  input  Reset_PC,
  input  Clock,
  input  Reset_REG
);

  wire and_1_out, and_2_out, control_unit_1_alusrc, control_unit_1_beq, control_unit_1_bneq,
       control_unit_1_jmp, control_unit_1_memread, control_unit_1_memtoreg, control_unit_1_memwrite,
       control_unit_1_regdst, control_unit_1_regwrite, n8_bit_alu_1_zero, not_1_out, or_1_out;
  wire [2:0] control_unit_1_aluop;
  wire [3:0] data_memory_1_output, multiplexer_3_out, multiplexer_5_out, n8_bit_alu_1_output,
       register_files_1_read_reg_1_2, register_files_1_read_reg_2_2;
  wire [4:4] n8_bit_alu_1_carry;
  wire [7:0] adder_1_out, adder_2_out, bit_extender_1_out, bit_extender_2_out, bit_extender_3_out,
       bit_extender_4_out, bit_extender_5_out, instrcution_memory_1_pc_output, multiplexer_1_out,
       multiplexer_2_out, multiplexer_4_out;
  wire [15:0] instrcution_memory_1_instruction_output;

  Multiplexer #(.width(8), .enable("false")) multiplexer_1 (
    .in0(multiplexer_4_out), .in1(instrcution_memory_1_instruction_output[11:4]), .out(multiplexer_1_out),
    .sel(control_unit_1_jmp));
  Instrcution_Memory instrcution_memory_1 (
    .PC_Input(multiplexer_1_out), .PC_Output(instrcution_memory_1_pc_output),
    .Instruction_Output(instrcution_memory_1_instruction_output), .Reset(Reset_PC), .Clock(Clock));
  assign bit_extender_1_out = {{4{1'b0}}, instrcution_memory_1_instruction_output[3:0]};  // Bit_Extender bit_extender_1
  assign bit_extender_2_out = {{4{1'b0}}, instrcution_memory_1_instruction_output[7:4]};  // Bit_Extender bit_extender_2
  assign bit_extender_3_out = {{4{1'b0}}, instrcution_memory_1_instruction_output[11:8]};  // Bit_Extender bit_extender_3
  Adder adder_1 (.a(instrcution_memory_1_pc_output), .b(8'h1), .out(adder_1_out));  // open: cin, cout
  Multiplexer #(.width(8), .enable("false")) multiplexer_2 (
    .in0(bit_extender_2_out), .in1(bit_extender_1_out), .out(multiplexer_2_out), .sel(control_unit_1_regdst));
  Register_Files register_files_1 (
    .Write_Reg_Addr(multiplexer_2_out), .Read_Reg_1(bit_extender_3_out), .Read_Reg_2(bit_extender_2_out),
    .Data_Write(multiplexer_5_out), .RegWrite(control_unit_1_regwrite),
    .Read_Reg_1_2(register_files_1_read_reg_1_2), .Read_Reg_2_2(register_files_1_read_reg_2_2),
    .Reset(Reset_REG), .Clock(Clock));
  Control_Unit control_unit_1 (
    .in_1(instrcution_memory_1_instruction_output[15:12]), .bneq(control_unit_1_bneq),
    .jmp(control_unit_1_jmp), .RegWrite(control_unit_1_regwrite), .AluSrc(control_unit_1_alusrc),
    .MemtoReg(control_unit_1_memtoreg), .MemWrite(control_unit_1_memwrite), .MemRead(control_unit_1_memread),
    .Beq(control_unit_1_beq), .RegDst(control_unit_1_regdst), .AluOP(control_unit_1_aluop));  // open: output
  Multiplexer #(.width(4), .enable("false")) multiplexer_3 (
    .in0(register_files_1_read_reg_2_2), .in1(instrcution_memory_1_instruction_output[3:0]),
    .out(multiplexer_3_out), .sel(control_unit_1_alusrc));
  assign bit_extender_4_out = {{4{instrcution_memory_1_instruction_output[3]}}, instrcution_memory_1_instruction_output[3:0]};  // Bit_Extender bit_extender_4
  not not_1 (not_1_out, n8_bit_alu_1_zero);
  and and_1 (and_1_out, control_unit_1_bneq, not_1_out);
  _8_bit_alu u_8_bit_alu_1 (
    .Alu_In_1(register_files_1_read_reg_1_2), .Alu_In_2(multiplexer_3_out), .Selection(control_unit_1_aluop),
    .\output (n8_bit_alu_1_output), .Carry(n8_bit_alu_1_carry[4]), .zero(n8_bit_alu_1_zero));
  Adder adder_2 (.a(adder_1_out), .b(bit_extender_4_out), .out(adder_2_out));  // open: cin, cout
  and and_2 (and_2_out, n8_bit_alu_1_zero, control_unit_1_beq);
  assign bit_extender_5_out = {{3{1'b0}}, {n8_bit_alu_1_carry[4], n8_bit_alu_1_output}};  // Bit_Extender bit_extender_5
  or or_1 (or_1_out, and_2_out, and_1_out);
  Multiplexer #(.width(8), .enable("false")) multiplexer_4 (
    .in0(adder_1_out), .in1(adder_2_out), .out(multiplexer_4_out), .sel(or_1_out));
  Data_Memory data_memory_1 (
    .Alu_Output_Address(bit_extender_5_out), .Data_to_Write(register_files_1_read_reg_2_2),
    .MemRead(control_unit_1_memread), .MemWrite(control_unit_1_memwrite), .Output(data_memory_1_output),
    .clock(Clock), .Reset(Reset_REG));
  Multiplexer #(.width(4), .enable("false")) multiplexer_5 (
    .in0(n8_bit_alu_1_output), .in1(data_memory_1_output), .out(multiplexer_5_out),
    .sel(control_unit_1_memtoreg));
endmodule

module _8_bit_alu (
  input  [3:0] Alu_In_1,
  input  [3:0] Alu_In_2,
  input  [2:0] Selection,
  output Carry,
  output zero,
  output [3:0] \output 
);

  wire [3:0] adder_1_out, and_1_out, nor_1_out, or_1_out, shifter_1_out, shifter_2_out, subtractor_1_out;

  Adder #(.width(4)) adder_1 (.a(Alu_In_1), .b(Alu_In_2), .out(adder_1_out), .cout(Carry));  // open: cin
  Subtractor #(.width(4)) subtractor_1 (.a(Alu_In_1), .b(Alu_In_2), .out(subtractor_1_out));  // open: bin, bout
  assign and_1_out = Alu_In_1 & Alu_In_2;  // AND_Gate and_1, 4 bits wide
  assign or_1_out = Alu_In_1 | Alu_In_2;  // OR_Gate or_1, 4 bits wide
  Shifter #(.width(4)) shifter_1 (.in(Alu_In_1), .\dist (Alu_In_2[1:0]), .out(shifter_1_out));
  Shifter #(.width(4), .shift("lr")) shifter_2 (.in(Alu_In_1), .\dist (Alu_In_2[1:0]), .out(shifter_2_out));
  assign nor_1_out = ~(Alu_In_1 | Alu_In_2);  // NOR_Gate nor_1, 4 bits wide
  Multiplexer #(.select(3), .width(4), .enable("false")) multiplexer_1 (
    .in0(adder_1_out), .in1(subtractor_1_out), .in2(and_1_out), .in3(or_1_out), .in4(shifter_1_out),
    .in5(shifter_2_out), .in6(nor_1_out), .in7(4'b0000), .out(\output ), .sel(Selection));
  nor nor_2 (zero, \output [0], \output [1], \output [2], \output [3]);
endmodule

module Control_Unit (
  input  [3:0] in_1,
  output bneq,
  output jmp,
  output RegWrite,
  output AluSrc,
  output MemtoReg,
  output MemWrite,
  output MemRead,
  output Beq,
  output RegDst,
  output [2:0] AluOP,
  output [11:0] \output 
);

  ROM #(.addrWidth(4), .dataWidth(12)) rom_1 (
    .addr(in_1), .data({AluOP, \output [8], Beq, MemRead, MemWrite, MemtoReg, AluSrc, \output [2], jmp, bneq}));  // open: sel

  assign {\output [11:9], \output [7:3], \output [1:0]} = {AluOP, Beq, MemRead, MemWrite, MemtoReg, AluSrc, jmp, bneq};
  assign RegDst = \output [8];
  assign RegWrite = \output [2];

  // Notes on the sheet:
  //   contents of rom_1 (hex, n*v repeats v):
  //   504 d04 80c 28 280 60c e02 704 201 40c 5c 104 a0c 20c c 304
endmodule

module Register_Files (
  input  [7:0] Write_Reg_Addr,
  input  [7:0] Read_Reg_1,
  input  [7:0] Read_Reg_2,
  input  [3:0] Data_Write,
  input  Reset,
  input  Clock,
  input  RegWrite,
  output [3:0] Read_Reg_1_2,
  output [3:0] Read_Reg_2_2
);

  wire and_1_out, and_2_out, and_3_out, and_4_out, and_5_out, and_6_out, and_7_out, decoder_1_out0,
       decoder_1_out1, decoder_1_out2, decoder_1_out3, decoder_1_out4, decoder_1_out5, decoder_1_out6;
  wire [3:0] sp_q, t0_q, t1_q, t2_q, t3_q, t4_q, zero_q;

  Decoder #(.select(3), .enable("false")) decoder_1 (
    .out0(decoder_1_out0), .out1(decoder_1_out1), .out2(decoder_1_out2), .out3(decoder_1_out3),
    .out4(decoder_1_out4), .out5(decoder_1_out5), .out6(decoder_1_out6), .sel(Write_Reg_Addr[2:0]));  // open: out7
  and and_1 (and_1_out, decoder_1_out0, RegWrite);
  and and_2 (and_2_out, decoder_1_out1, RegWrite);
  and and_3 (and_3_out, decoder_1_out2, RegWrite);
  and and_4 (and_4_out, decoder_1_out3, RegWrite);
  and and_5 (and_5_out, decoder_1_out4, RegWrite);
  and and_6 (and_6_out, decoder_1_out5, RegWrite);
  Register #(.width(4), .trigger("falling")) zero (.D(4'b0000), .en(and_1_out), .Q(zero_q), .clk(Clock), .clr(Reset));
  Register #(.width(4), .trigger("falling")) t0 (.D(Data_Write), .en(and_2_out), .Q(t0_q), .clk(Clock), .clr(Reset));
  Register #(.width(4), .trigger("falling")) t1 (.D(Data_Write), .en(and_3_out), .Q(t1_q), .clk(Clock), .clr(Reset));
  Register #(.width(4), .trigger("falling")) t2 (.D(Data_Write), .en(and_4_out), .Q(t2_q), .clk(Clock), .clr(Reset));
  Register #(.width(4), .trigger("falling")) t3 (.D(Data_Write), .en(and_5_out), .Q(t3_q), .clk(Clock), .clr(Reset));
  Register #(.width(4), .trigger("falling")) t4 (.D(Data_Write), .en(and_6_out), .Q(t4_q), .clk(Clock), .clr(Reset));
  and and_7 (and_7_out, decoder_1_out6, RegWrite);
  Register #(.width(4), .trigger("falling")) sp (.D(Data_Write), .en(and_7_out), .Q(sp_q), .clk(Clock), .clr(Reset));
  Multiplexer #(.select(3), .width(4), .disabled(0), .enable("false")) multiplexer_1 (
    .in0(zero_q), .in1(t0_q), .in2(t1_q), .in3(t2_q), .in4(t3_q), .in5(t4_q), .in6(sp_q), .in7(4'b0000),
    .out(Read_Reg_1_2), .sel(Read_Reg_1[2:0]));
  Multiplexer #(.select(3), .width(4), .enable("false")) multiplexer_2 (
    .in0(zero_q), .in1(t0_q), .in2(t1_q), .in3(t2_q), .in4(t3_q), .in5(t4_q), .in6(sp_q), .in7(4'b0000),
    .out(Read_Reg_2_2), .sel(Read_Reg_2[2:0]));
endmodule

module Data_Memory (
  input  [7:0] Alu_Output_Address,
  input  [3:0] Data_to_Write,
  input  clock,
  input  MemRead,
  input  MemWrite,
  input  Reset,
  output [3:0] Output
);

  wire not_1_out;

  not not_1 (not_1_out, clock);
  RAM #(.dataWidth(4), .bus("separate")) ram_1 (
    .addr(Alu_Output_Address), .din(Data_to_Write), .data(Output), .str(MemWrite), .clk(not_1_out),
    .ld(MemRead), .clr(Reset));  // open: sel
endmodule

module Instrcution_Memory (
  input  [7:0] PC_Input,
  input  Reset,
  input  Clock,
  output [7:0] PC_Output,
  output [15:0] Instruction_Output
);

  Register register_1 (.D(PC_Input), .en(1'b1), .Q(PC_Output), .clk(Clock), .clr(Reset));
  ROM #(.dataWidth(16)) rom_1 (.addr(PC_Output), .data(Instruction_Output));  // open: sel
  Register #(.width(16)) register_2 (.clk(Clock), .clr(Reset));  // open: D, en, Q

  // Notes on the sheet:
  //   contents of rom_1 (hex, n*v repeats v):
  //   0 e66f e023 e034 d332 b231 f234 1135 3323 c331 4431 61b0 2441 a334 3620 d661 3630 d661 61a0 5225
  //   e661 a630 352 e661 a620 61b0 8318 7131 9531
endmodule
